# Fritzing sketch iCAT_v1 (saved by Fritzing 0.9.3b)
circuit board: 8.46667cm x 5.64444cm

parts:
  RFID1 = ArduCam
  Part1 = Arduino Uno (Rev3)
  Zeiss_trigger_OUT = Power plug
  C1_100uF1 = Electrolytic Capacitor [capacitance=1µF package="100 mil [THT, electrolytic]"]
  M2 = Stepper Motor - Unipolar
  M3 = xy-mos d4184 [package=THT]
  MD09B1 = Pololu A4988 [package=SO16]
  LED1 = LEDs [package=led10mm]
  M4 = xy-mos d4184 [package=THT]
  Main_Power_12V = Power plug
  S1 = SWITCH-SPST-2 [package=switch-spst-vertical]
  Pololu_A1 = Pololu A4988 [package=SO16]
  4_7kΩ = Resistor [tolerance=±5% resistance=4.7k package="0402 [SMD]"]
  Peltiere = Peltier Element
  J2 = Power Jack [package=power_jack_slot]
  J3 = Power Plug
  M5 = Stepper Motor - Unipolar
  10k_NTC = Temperature Sensor (Thermistor) [thermistor_type=NTC package=THT]  # not connected

nets (from the breadboard view):
  N1: RFID1.CS, Part1.D10_PWM/SS
  N2: RFID1.MOSI, Part1.D11_PWM/MOSI
  N3: RFID1.MISO, Part1.D12/MISO
  N4: RFID1.SCK, Part1.D13/SCK
  VDD: RFID1.VCC, Part1.5V, MD09B1.MS1, MD09B1.MS2, MD09B1.MS3, MD09B1.VDD, Pololu_A1.MS1, Pololu_A1.MS2, Pololu_A1.MS3, Pololu_A1.VDD
  GND: RFID1.GND, Part1.GND, Zeiss_trigger_OUT.GND, M3.GND#1, M3.LOAD, MD09B1.GND#8, LED1.C, M4.GND#1, M4.LOAD, Pololu_A1.GND#8, 4_7kΩ.Pin_1, J2.GNDBREAK
  N5: RFID1.SDA, Part1.A4/SDA
  N6: RFID1.SCL, Part1.A5/SCL
  N7: Part1.A1, Zeiss_trigger_OUT.VCC, 4_7kΩ.Pin_0
  N8: Part1.D8, Pololu_A1.DIR
  GND_2: Part1.D9_PWM, Part1.D6_PWM, C1_100uF1.-, C1_100uF1.+, M3.PWM, M3.GND#2, M3.+, MD09B1.GND#14, MD09B1.VMOT, LED1.A, M4.PWM, M4.GND#2, M4.+, Main_Power_12V.GND, S1.P, Pololu_A1.GND#14, Pololu_A1.VMOT, Peltiere.pin1, J2.GND, J2.tip_GND, J3.GND, J3.tip_GND
  N9: Part1.D3_PWM, Pololu_A1.STEP
  N10: Part1.D4, MD09B1.DIR
  N11: Part1.D5_PWM, MD09B1.STEP
  N12: Part1.D7, MD09B1.ENABLE, Pololu_A1.ENABLE
  N13: M2.A, MD09B1.2B
  N14: M2.C, MD09B1.2A
  N15: M2.B, MD09B1.1A
  N16: M2.D, MD09B1.1B
  N17: MD09B1.RESET, MD09B1.SLEEP
  N18: Main_Power_12V.VCC, S1.O
  N19: Pololu_A1.RESET, Pololu_A1.SLEEP
  N20: Pololu_A1.1B, M5.D
  N21: Pololu_A1.1A, M5.B
  N22: Pololu_A1.2A, M5.C
  N23: Pololu_A1.2B, M5.A
  N24: Peltiere.pin2, J2.PWR, J2.tip_PWR, J3.PWR, J3.tip_PWR

custom parts:
  ArduCam: 5 MINI plus
  xy-mos d4184: xy-mos d4184 Two parallel N-Channel logic compatible MOSFETS with low Rds(on) for high current low-side switching applications.
  Power Jack: Power Jack This is the standard 5.5mm barrel jack for power. Ths one is modified to mate with the barrel plug part and allow the two to "connect" so batteries and wall warts can be "connected" in breadboard and will go through to schematic.
  Power Plug: Power Jack This is the standard 5.5mm barrel plug for power. This part has bendable leads (i.e. wires in the real world) to connect to wall warts or the breadboard in the standard wire end, and hidden connectors on the tip end that will connect when "plugged in" (overlapped with the jack so it appears "plugged in" in breadboard) to the modified coax jack part. Internal busses connect the two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
