# Fritzing sketch iCat_v2-landscape (saved by Fritzing 0.9.3b)

parts:
  RFID1 = ArduCam
  Part2 = Arduino Uno (Rev3)  # not connected
  DRV_1 = Pololu DRV 8825 Stepper Motor Carrier, High Current [package=SO16]  # not connected
  Main_Power_12V = Power plug
  J4 = Power Jack [package=power_jack_slot]
  J5 = Power Plug
  Peltier_module = Peltier Element
  Part4 = ws2812b [package="smd 2812b"]
  4_7_kΩ = Resistor [tolerance=±5% resistance=4.7k package="0402 [SMD]"]
  Camera_motor = Stepper Motor - Unipolar
  Axial_motor = Stepper Motor - Unipolar
  DRV_2 = Pololu DRV 8825 Stepper Motor Carrier, High Current [package=SO16]
  Arduino_CNC_Shield_V3_00_2 = Arduino_CNC_V3.00
  10kΩ = Resistor [tolerance=±5% resistance=10k package="0402 [SMD]"]
  10k_NTC = Temperature Sensor (Thermistor) [thermistor_type=NTC package=THT]
  Trigger_IN = Power plug
  U1 = POT [package=pot_alpha_rv16af-20]
  Part5 = IFR520 MOS module [package=THT]

nets:
  N1: RFID1.CS, Arduino_CNC_Shield_V3_00_2.End_Stops_Y+_(and_Y-)
  N2: RFID1.MOSI, Arduino_CNC_Shield_V3_00_2.End_Stops_Z+_(and_Z-)_/_SpnEn
  N3: RFID1.MISO, Arduino_CNC_Shield_V3_00_2.SpnEn_/_Z_Limit
  N4: RFID1.SCK, Arduino_CNC_Shield_V3_00_2.SpnDir
  N5: RFID1.VCC, Arduino_CNC_Shield_V3_00_2.5V#75, 10kΩ.Pin_0, Part5.pin2
  N6: RFID1.GND, Arduino_CNC_Shield_V3_00_2.CoolEn_(Gnd)
  N7: RFID1.SDA, Arduino_CNC_Shield_V3_00_2.SDA
  N8: RFID1.SCL, Arduino_CNC_Shield_V3_00_2.SCL_/_Probe
  N9: Main_Power_12V.GND, Arduino_CNC_Shield_V3_00_2.POWER_-, Part5.pin5
  N10: Main_Power_12V.VCC, Arduino_CNC_Shield_V3_00_2.POWER_+, Arduino_CNC_Shield_V3_00_2.Hold_(Gnd), Part5.pin4
  GND: J4.GND, J4.tip_GND, J5.GND, J5.tip_GND, Peltier_module.pin1, Part5.pin7
  N11: J4.PWR, J4.tip_PWR, J5.PWR, J5.tip_PWR, Peltier_module.pin2
  N12: J4.GNDBREAK, Part5.pin6
  N13: Part4.VDD, Arduino_CNC_Shield_V3_00_2.5V#11
  VSS: Part4.VSS, Arduino_CNC_Shield_V3_00_2.GND
  N14: Part4.DIN, DRV_2.MS2, Arduino_CNC_Shield_V3_00_2.Y.DIR
  N15: 4_7_kΩ.Pin_0, Arduino_CNC_Shield_V3_00_2.Hold, Trigger_IN.VCC
  N16: 4_7_kΩ.Pin_1, Arduino_CNC_Shield_V3_00_2.End_Stops_X-_(Gnd), Trigger_IN.GND
  N17: Camera_motor.A, Arduino_CNC_Shield_V3_00_2.Z-MTR_'1'
  N18: Camera_motor.C, Arduino_CNC_Shield_V3_00_2.Z-MTR_'2'
  N19: Camera_motor.B, Arduino_CNC_Shield_V3_00_2.Z-MTR_'3'
  N20: Camera_motor.D, Arduino_CNC_Shield_V3_00_2.Z-MTR_'4'
  N21: Axial_motor.A, Arduino_CNC_Shield_V3_00_2.X-MTR_'1'
  N22: Axial_motor.C, Arduino_CNC_Shield_V3_00_2.X-MTR_'2'
  N23: Axial_motor.B, Arduino_CNC_Shield_V3_00_2.X-MTR_'3'
  N24: Axial_motor.D, Arduino_CNC_Shield_V3_00_2.X-MTR_'4'
  N25: Arduino_CNC_Shield_V3_00_2.Y.STEP, U1.S
  N26: Arduino_CNC_Shield_V3_00_2.X_-_M2, Arduino_CNC_Shield_V3_00_2.X_-_M2_(5V)
  N27: Arduino_CNC_Shield_V3_00_2.Z_-_M2, Arduino_CNC_Shield_V3_00_2.Z_-_M2_(5V)
  N28: Arduino_CNC_Shield_V3_00_2.Abort, 10kΩ.Pin_1, 10k_NTC.pin_1
  N29: Arduino_CNC_Shield_V3_00_2.Resume_(Gnd), 10k_NTC.pin_0
  N30: Arduino_CNC_Shield_V3_00_2.E-STOP_(Gnd), Part5.pin3
  N31: U1.E, Part5.pin1

custom parts:
  ArduCam: 5 MINI plus
  Pololu DRV 8825 Stepper Motor Carrier, High Current: DRV 8825 This is a Stepper Motor Controller for integrated circuits. This breakout board for TI’s DRV8825 microstepping bipolar stepper motor driver features adjustable current limiting, over-current and over-temperature protection, and six microstep resolutions (down to 1/32-step). It operates from 8.2 V to 45 V and can deliver up to approximately 1.5 A per phase without a heat sink or forced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
  Power Jack: Power Jack This is the standard 5.5mm barrel jack for power. Ths one is modified to mate with the barrel plug part and allow the two to "connect" so batteries and wall warts can be "connected" in breadboard and will go through to schematic.
  Power Plug: Power Jack This is the standard 5.5mm barrel plug for power. This part has bendable leads (i.e. wires in the real world) to connect to wall warts or the breadboard in the standard wire end, and hidden connectors on the tip end that will connect when "plugged in" (overlapped with the jack so it appears "plugged in" in breadboard) to the modified coax jack part. Internal busses connect the two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
  Arduino_CNC_V3.00: Protoneer Arduino CNC Shield V3.00 If using Grbl V0.9: The “A” axis can not be used (yet). The “SCL” (Arduino A5) pin is now used for 'Probing' input. The “End Stops Z+ & Z-” (Arduino D11) and “SpnEn” (Arduino D12) have been switched!
